// Logisim project 7_Segment_Calculator.circ as structural Verilog: 24 circuits, main circuit NOT
module main (
  input  B,
  input  A,
  input  in_3,
  input  in_4,
  input  in_5,
  input  in_6,
  input  in_7,
  input  Add_Sub,
  input  in_9
);

  wire a_d0_1_out_5, a_d1_1_out_5, b_d0_1_out_5, c_d0_1_out_5, d_d0_1_out_5, d_d1_1_out_5, e_d0_1_out_5,
       e_d1_1_out_5, f_d0_1_out_5, f_d1_1_out_5, g_d0_1_out_5, n4_bit_arithmetic_1_ovreflow,
       n4_bit_arithmetic_1_s0, n4_bit_arithmetic_1_s1, n4_bit_arithmetic_1_s2, n4_bit_arithmetic_1_s3;

  _4_bit_arithmetic u_4_bit_arithmetic_1 (
    .A3(B), .B3(A), .in_3(in_3), .B2(in_4), .in_5(in_5), .B1(in_6), .in_7(in_7), .B0(Add_Sub),
    .ADD_SUB(in_9), .Ovreflow(n4_bit_arithmetic_1_ovreflow), .S3(n4_bit_arithmetic_1_s3),
    .S2(n4_bit_arithmetic_1_s2), .S1(n4_bit_arithmetic_1_s1), .S0(n4_bit_arithmetic_1_s0));
  a_d1 a_d1_1 (
    .in_1(n4_bit_arithmetic_1_s3), .in_2(n4_bit_arithmetic_1_s2), .in_3(n4_bit_arithmetic_1_s1),
    .in_4(n4_bit_arithmetic_1_s0), .out_5(a_d1_1_out_5));
  d_d1 d_d1_1 (
    .in_1(n4_bit_arithmetic_1_s3), .in_2(n4_bit_arithmetic_1_s2), .in_3(n4_bit_arithmetic_1_s1),
    .in_4(n4_bit_arithmetic_1_s0), .out_5(d_d1_1_out_5));
  e_d1 e_d1_1 (
    .in_1(n4_bit_arithmetic_1_s3), .in_2(n4_bit_arithmetic_1_s2), .in_3(n4_bit_arithmetic_1_s1),
    .in_4(n4_bit_arithmetic_1_s0), .out_5(e_d1_1_out_5));
  f_d1 f_d1_1 (
    .in_1(n4_bit_arithmetic_1_s3), .in_2(n4_bit_arithmetic_1_s2), .in_3(n4_bit_arithmetic_1_s1),
    .in_4(n4_bit_arithmetic_1_s0), .out_5(f_d1_1_out_5));
  _7_Segment_Display u_7_segment_display_1 (
    .g(n4_bit_arithmetic_1_ovreflow), .f(n4_bit_arithmetic_1_ovreflow), .a(n4_bit_arithmetic_1_ovreflow),
    .e(n4_bit_arithmetic_1_ovreflow), .d(n4_bit_arithmetic_1_ovreflow));  // open: b, c, dp
  _7_Segment_Display u_7_segment_display_2 (
    .g(n4_bit_arithmetic_1_ovreflow), .b(n4_bit_arithmetic_1_ovreflow), .e(n4_bit_arithmetic_1_ovreflow),
    .d(n4_bit_arithmetic_1_ovreflow), .c(n4_bit_arithmetic_1_ovreflow));  // open: f, a, dp
  a_d0 a_d0_1 (
    .in_1(n4_bit_arithmetic_1_s3), .in_2(n4_bit_arithmetic_1_s2), .in_3(n4_bit_arithmetic_1_s1),
    .in_4(n4_bit_arithmetic_1_s0), .out_5(a_d0_1_out_5));
  b_d0 b_d0_1 (
    .in_1(n4_bit_arithmetic_1_s3), .in_2(n4_bit_arithmetic_1_s2), .in_3(n4_bit_arithmetic_1_s1),
    .in_4(n4_bit_arithmetic_1_s0), .out_5(b_d0_1_out_5));
  c_d0 c_d0_1 (
    .in_1(n4_bit_arithmetic_1_s3), .in_2(n4_bit_arithmetic_1_s2), .in_3(n4_bit_arithmetic_1_s1),
    .in_4(n4_bit_arithmetic_1_s0), .out_5(c_d0_1_out_5));
  d_d0 d_d0_1 (
    .in_1(n4_bit_arithmetic_1_s3), .in_2(n4_bit_arithmetic_1_s2), .in_3(n4_bit_arithmetic_1_s1),
    .in_4(n4_bit_arithmetic_1_s0), .out_5(d_d0_1_out_5));
  e_d0 e_d0_1 (
    .in_1(n4_bit_arithmetic_1_s3), .in_2(n4_bit_arithmetic_1_s2), .in_3(n4_bit_arithmetic_1_s1),
    .in_4(n4_bit_arithmetic_1_s0), .out_5(e_d0_1_out_5));
  f_d0 f_d0_1 (
    .in_1(n4_bit_arithmetic_1_s3), .in_2(n4_bit_arithmetic_1_s2), .in_3(n4_bit_arithmetic_1_s1),
    .in_4(n4_bit_arithmetic_1_s0), .out_5(f_d0_1_out_5));
  g_d0 g_d0_1 (
    .in_1(n4_bit_arithmetic_1_s3), .in_2(n4_bit_arithmetic_1_s2), .in_3(n4_bit_arithmetic_1_s1),
    .in_4(n4_bit_arithmetic_1_s0), .out_5(g_d0_1_out_5));
  _7_Segment_Display u_7_segment_display_3 (
    .g(n4_bit_arithmetic_1_ovreflow), .b(n4_bit_arithmetic_1_ovreflow), .e(n4_bit_arithmetic_1_ovreflow),
    .d(n4_bit_arithmetic_1_ovreflow), .c(n4_bit_arithmetic_1_ovreflow), .dp(n4_bit_arithmetic_1_ovreflow));  // open: f, a
  _7_Segment_Display u_7_segment_display_4 (
    .g(n4_bit_arithmetic_1_ovreflow), .f(n4_bit_arithmetic_1_ovreflow), .a(n4_bit_arithmetic_1_ovreflow),
    .b(n4_bit_arithmetic_1_ovreflow), .e(n4_bit_arithmetic_1_ovreflow), .c(n4_bit_arithmetic_1_ovreflow));  // open: d, dp
  _7_Segment_Display u_7_segment_display_5 (
    .g(1'b0), .f(f_d1_1_out_5), .a(a_d1_1_out_5), .b(1'b1), .e(e_d1_1_out_5), .d(d_d1_1_out_5), .c(1'b1));  // open: dp
  _7_Segment_Display u_7_segment_display_6 (.g(n4_bit_arithmetic_1_s3));  // open: f, a, b, e, d, c, dp
  _7_Segment_Display u_7_segment_display_7 (
    .g(g_d0_1_out_5), .f(f_d0_1_out_5), .a(a_d0_1_out_5), .b(b_d0_1_out_5), .e(e_d0_1_out_5),
    .d(d_d0_1_out_5), .c(c_d0_1_out_5));  // open: dp

  // Notes on the sheet:
  //   D1
  //   a
  //   d
  //   e
  //   f
  //   D0
  //   a
  //   b
  //   c
  //   d
  //   e
  //   f
  //   g
endmodule

module NOT (
  input  in_1,
  output out_2
);

  Transistor transistor_1 (.in(1'b1), .out(out_2), .gate(in_1));
  Transistor #(.\type ("n")) transistor_2 (.in(1'b0), .out(out_2), .gate(in_1));

  // Notes on the sheet:
  //   NOT
endmodule

module NAND (
  input  in_1,
  input  in_2,
  output out_3
);

  wire transistor_3_out;

  Transistor transistor_1 (.in(1'b1), .out(out_3), .gate(in_1));
  Transistor #(.\type ("n")) transistor_2 (.in(transistor_3_out), .out(out_3), .gate(in_1));
  Transistor #(.\type ("n")) transistor_3 (.in(1'b0), .out(transistor_3_out), .gate(in_2));
  Transistor transistor_4 (.in(1'b1), .out(out_3), .gate(in_2));

  // Notes on the sheet:
  //   NAND
endmodule

module NOR (
  input  in_1,
  input  in_2,
  output out_3
);

  wire transistor_2_out;

  AND and_1 ();  // open: in_1, in_2, out_3
  Transistor #(.\type ("n")) transistor_1 (.in(1'b0), .out(out_3), .gate(in_1));
  Transistor transistor_2 (.in(1'b1), .out(transistor_2_out), .gate(in_1));
  Transistor transistor_3 (.in(transistor_2_out), .out(out_3), .gate(in_2));
  Transistor #(.\type ("n")) transistor_4 (.in(1'b0), .out(out_3), .gate(in_2));

  // Notes on the sheet:
  //   NOR
endmodule

module AND (
  input  in_1,
  input  in_2,
  output out_3
);

  wire transistor_1_out, transistor_3_out;

  Transistor transistor_1 (.in(1'b1), .out(transistor_1_out), .gate(in_1));
  Transistor #(.\type ("n")) transistor_2 (.in(transistor_3_out), .out(transistor_1_out), .gate(in_1));
  Transistor #(.\type ("n")) transistor_3 (.in(1'b0), .out(transistor_3_out), .gate(in_2));
  Transistor transistor_4 (.in(1'b1), .out(transistor_1_out), .gate(in_2));
  Transistor transistor_5 (.in(1'b1), .out(out_3), .gate(transistor_1_out));
  Transistor #(.\type ("n")) transistor_6 (.in(1'b0), .out(out_3), .gate(transistor_1_out));

  // Notes on the sheet:
  //   AND
endmodule

module OR (
  input  in_1,
  input  in_2,
  output out_3
);

  wire transistor_1_out, transistor_2_out;

  Transistor #(.\type ("n")) transistor_1 (.in(1'b0), .out(transistor_1_out), .gate(in_1));
  Transistor transistor_2 (.in(1'b1), .out(transistor_2_out), .gate(in_1));
  Transistor transistor_3 (.in(transistor_2_out), .out(transistor_1_out), .gate(in_2));
  Transistor transistor_4 (.in(1'b1), .out(out_3), .gate(transistor_1_out));
  Transistor #(.\type ("n")) transistor_5 (.in(1'b0), .out(out_3), .gate(transistor_1_out));
  Transistor #(.\type ("n")) transistor_6 (.in(1'b0), .out(transistor_1_out), .gate(in_2));
endmodule

module XOR (
  input  in_1,
  input  in_2,
  output out_3
);

  wire nand_1_out_3, or_1_out_3;

  NAND nand_1 (.in_1(in_1), .in_2(in_2), .out_3(nand_1_out_3));
  OR or_1 (.in_1(in_1), .in_2(in_2), .out_3(or_1_out_3));
  AND and_1 (.in_1(nand_1_out_3), .in_2(or_1_out_3), .out_3(out_3));

  // Notes on the sheet:
  //   XOR
endmodule

module half_adder (
  input  in_1,
  input  in_2,
  output out_3,
  output out_4
);

  AND and_1 (.in_1(in_1), .in_2(in_2), .out_3(out_3));
  XOR xor_1 (.in_1(in_1), .in_2(in_2), .out_3(out_4));
endmodule

module full_adder (
  input  in_1,
  input  in_2,
  input  in_3,
  output out_4,
  output out_5
);

  wire half_adder_1_out_3, half_adder_1_out_4, half_adder_2_out_3;

  half_adder half_adder_1 (.in_1(in_1), .in_2(in_2), .out_3(half_adder_1_out_3), .out_4(half_adder_1_out_4));
  half_adder half_adder_2 (.in_1(in_3), .in_2(half_adder_1_out_4), .out_3(half_adder_2_out_3), .out_4(out_5));
  OR or_1 (.in_1(half_adder_1_out_3), .in_2(half_adder_2_out_3), .out_3(out_4));
endmodule

module _4_bit_adder (
  input  in_1,
  input  in_2,
  input  in_3,
  input  in_4,
  input  in_5,
  input  in_6,
  input  in_7,
  input  in_8,
  input  in_9,
  output out_10,
  output out_11,
  output out_12,
  output out_13,
  output out_14
);

  wire full_adder_2_out_4, full_adder_3_out_4, full_adder_4_out_4;

  full_adder full_adder_1 (.in_1(in_1), .in_2(in_2), .in_3(full_adder_2_out_4), .out_4(out_10), .out_5(out_11));
  full_adder full_adder_2 (
    .in_1(in_3), .in_2(in_4), .in_3(full_adder_3_out_4), .out_4(full_adder_2_out_4), .out_5(out_12));
  full_adder full_adder_3 (
    .in_1(in_5), .in_2(in_6), .in_3(full_adder_4_out_4), .out_4(full_adder_3_out_4), .out_5(out_13));
  full_adder full_adder_4 (.in_1(in_7), .in_2(in_8), .in_3(in_9), .out_4(full_adder_4_out_4), .out_5(out_14));
endmodule

module _4_bit_subtractor (
  input  in_1,
  input  in_2,
  input  in_3,
  input  in_4,
  input  in_5,
  input  in_6,
  input  in_7,
  input  in_8,
  output out_9,
  output out_10,
  output out_11,
  output out_12,
  output out_13
);

  wire full_adder_2_out_4, full_adder_3_out_4, full_adder_4_out_4, not_1_out_2, not_2_out_2, not_3_out_2,
       not_4_out_2;

  NOT not_1 (.in_1(in_2), .out_2(not_1_out_2));
  NOT not_2 (.in_1(in_4), .out_2(not_2_out_2));
  NOT not_3 (.in_1(in_6), .out_2(not_3_out_2));
  NOT not_4 (.in_1(in_8), .out_2(not_4_out_2));
  full_adder full_adder_1 (.in_1(in_1), .in_2(not_1_out_2), .in_3(full_adder_2_out_4), .out_4(out_9), .out_5(out_10));
  full_adder full_adder_2 (
    .in_1(in_3), .in_2(not_2_out_2), .in_3(full_adder_3_out_4), .out_4(full_adder_2_out_4), .out_5(out_11));
  full_adder full_adder_3 (
    .in_1(in_5), .in_2(not_3_out_2), .in_3(full_adder_4_out_4), .out_4(full_adder_3_out_4), .out_5(out_12));
  full_adder full_adder_4 (.in_1(in_7), .in_2(not_4_out_2), .in_3(1'b1), .out_4(full_adder_4_out_4), .out_5(out_13));
endmodule

module mux (
  input  in_1,
  input  in_2,
  input  in_3,
  output out_4
);

  wire transistor_3_out, transistor_4_out, transistor_5_out, transistor_6_out;

  Transistor #(.\type ("n")) transistor_1 (.in(in_2), .out(out_4), .gate(in_1));
  Transistor transistor_2 (.in(in_3), .out(out_4), .gate(in_1));
  Transistor transistor_3 (.in(out_4), .out(transistor_3_out), .gate(in_1));
  Transistor transistor_4 (.in(transistor_3_out), .out(transistor_4_out), .gate(in_3));
  Transistor #(.\type ("n")) transistor_5 (.in(out_4), .out(transistor_5_out), .gate(in_1));
  Transistor transistor_6 (.in(transistor_5_out), .out(transistor_6_out), .gate(out_4));
  // also tied to GND on the sheet: {transistor_4_out, transistor_6_out}
endmodule

module _4_bit_arithmetic (
  input  A3,
  input  B3,
  input  in_3,
  input  B2,
  input  in_5,
  input  B1,
  input  in_7,
  input  B0,
  input  ADD_SUB,
  output Ovreflow,
  output S3,
  output S2,
  output S1,
  output S0
);

  wire full_adder_1_out_4, full_adder_2_out_4, full_adder_3_out_4, full_adder_4_out_4, mux_1_out_4,
       mux_2_out_4, mux_3_out_4, mux_4_out_4, not_1_out_2, not_2_out_2, not_3_out_2, not_4_out_2;

  NOT not_1 (.in_1(B3), .out_2(not_1_out_2));
  NOT not_2 (.in_1(B2), .out_2(not_2_out_2));
  NOT not_3 (.in_1(B1), .out_2(not_3_out_2));
  NOT not_4 (.in_1(B0), .out_2(not_4_out_2));
  mux mux_1 (.in_1(ADD_SUB), .in_2(not_1_out_2), .in_3(B3), .out_4(mux_1_out_4));
  mux mux_2 (.in_1(ADD_SUB), .in_2(not_2_out_2), .in_3(B2), .out_4(mux_2_out_4));
  mux mux_3 (.in_1(ADD_SUB), .in_2(not_3_out_2), .in_3(B1), .out_4(mux_3_out_4));
  mux mux_4 (.in_1(ADD_SUB), .in_2(not_4_out_2), .in_3(B0), .out_4(mux_4_out_4));
  full_adder full_adder_1 (
    .in_1(A3), .in_2(mux_1_out_4), .in_3(full_adder_2_out_4), .out_4(full_adder_1_out_4), .out_5(S3));
  full_adder full_adder_2 (
    .in_1(in_3), .in_2(mux_2_out_4), .in_3(full_adder_3_out_4), .out_4(full_adder_2_out_4), .out_5(S2));
  full_adder full_adder_3 (
    .in_1(in_5), .in_2(mux_3_out_4), .in_3(full_adder_4_out_4), .out_4(full_adder_3_out_4), .out_5(S1));
  full_adder full_adder_4 (.in_1(in_7), .in_2(mux_4_out_4), .in_3(ADD_SUB), .out_4(full_adder_4_out_4), .out_5(S0));
  XOR xor_1 (.in_1(full_adder_1_out_4), .in_2(full_adder_2_out_4), .out_3(Ovreflow));

  // Notes on the sheet:
  //   A2
  //   A1
  //   A0
endmodule

module a_d1 (
  input  in_1,
  input  in_2,
  input  in_3,
  input  in_4,
  output out_5
);

  wire and_1_out_3, and_2_out_3, nor_1_out_3, not_1_out_2, not_2_out_2, or_1_out_3, or_2_out_3;

  NOR nor_1 (.in_1(in_1), .in_2(in_2), .out_3(nor_1_out_3));
  NOT not_1 (.in_1(in_3), .out_2(not_1_out_2));
  NOT not_2 (.in_1(in_4), .out_2(not_2_out_2));
  OR or_1 (.in_1(nor_1_out_3), .in_2(and_1_out_3), .out_3(or_1_out_3));
  AND and_1 (.in_1(in_2), .in_2(not_1_out_2), .out_3(and_1_out_3));
  AND and_2 (.in_1(in_3), .in_2(or_2_out_3), .out_3(and_2_out_3));
  OR or_2 (.in_1(in_1), .in_2(not_2_out_2), .out_3(or_2_out_3));
  OR or_3 (.in_1(or_1_out_3), .in_2(and_2_out_3), .out_3(out_5));
endmodule

module a_d0 (
  input  in_1,
  input  in_2,
  input  in_3,
  input  in_4,
  output out_5
);

  wire and_1_out_3, and_2_out_3, and_3_out_3, and_4_out_3, and_5_out_3, and_6_out_3, not_1_out_2,
       not_2_out_2, not_3_out_2, not_4_out_2, or_1_out_3, or_2_out_3, or_3_out_3, xor_1_out_3;

  NOT not_1 (.in_1(in_1), .out_2(not_1_out_2));
  NOT not_2 (.in_1(in_2), .out_2(not_2_out_2));
  NOT not_3 (.in_1(in_3), .out_2(not_3_out_2));
  NOT not_4 (.in_1(in_4), .out_2(not_4_out_2));
  AND and_1 (.in_1(not_1_out_2), .in_2(not_2_out_2), .out_3(and_1_out_3));
  AND and_2 (.in_1(and_1_out_3), .in_2(not_4_out_2), .out_3(and_2_out_3));
  AND and_3 (.in_1(in_1), .in_2(in_4), .out_3(and_3_out_3));
  OR or_1 (.in_1(and_3_out_3), .in_2(and_2_out_3), .out_3(or_1_out_3));
  XOR xor_1 (.in_1(in_1), .in_2(in_2), .out_3(xor_1_out_3));
  AND and_4 (.in_1(or_1_out_3), .in_2(not_3_out_2), .out_3(and_4_out_3));
  OR or_2 (.in_1(not_1_out_2), .in_2(not_4_out_2), .out_3(or_2_out_3));
  AND and_5 (.in_1(or_2_out_3), .in_2(in_3), .out_3(and_5_out_3));
  AND and_6 (.in_1(xor_1_out_3), .in_2(in_4), .out_3(and_6_out_3));
  OR or_3 (.in_1(and_4_out_3), .in_2(and_5_out_3), .out_3(or_3_out_3));
  OR or_4 (.in_1(and_6_out_3), .in_2(or_3_out_3), .out_3(out_5));
endmodule

module b_d0 (
  input  in_1,
  input  in_2,
  input  in_3,
  input  in_4,
  output out_5
);

  wire and_1_out_3, and_2_out_3, and_3_out_3, nor_1_out_3, not_1_out_2, not_2_out_2, or_1_out_3, or_2_out_3,
       or_3_out_3;

  OR or_1 (.in_1(in_1), .in_2(not_2_out_2), .out_3(or_1_out_3));
  NOT not_1 (.in_1(in_3), .out_2(not_1_out_2));
  NOT not_2 (.in_1(in_4), .out_2(not_2_out_2));
  NOR nor_1 (.in_1(in_1), .in_2(in_2), .out_3(nor_1_out_3));
  AND and_1 (.in_1(or_1_out_3), .in_2(not_1_out_2), .out_3(and_1_out_3));
  AND and_2 (.in_1(in_3), .in_2(in_4), .out_3(and_2_out_3));
  OR or_2 (.in_1(nor_1_out_3), .in_2(and_1_out_3), .out_3(or_2_out_3));
  OR or_3 (.in_1(in_1), .in_2(and_2_out_3), .out_3(or_3_out_3));
  AND and_3 (.in_1(or_3_out_3), .in_2(in_2), .out_3(and_3_out_3));
  OR or_4 (.in_1(or_2_out_3), .in_2(and_3_out_3), .out_3(out_5));
endmodule

module c_d0 (
  input  in_1,
  input  in_2,
  input  in_3,
  input  in_4,
  output out_5
);

  wire not_1_out_2, or_1_out_3, xor_1_out_3;

  XOR xor_1 (.in_1(in_1), .in_2(in_2), .out_3(xor_1_out_3));
  NOT not_1 (.in_1(in_3), .out_2(not_1_out_2));
  OR or_1 (.in_1(not_1_out_2), .in_2(in_4), .out_3(or_1_out_3));
  OR or_2 (.in_1(xor_1_out_3), .in_2(or_1_out_3), .out_3(out_5));
endmodule

module d_d1 (
  input  in_1,
  input  in_2,
  input  in_3,
  input  in_4,
  output out_5
);

  wire and_1_out_3, and_2_out_3, nor_1_out_3, not_1_out_2, not_2_out_2, or_1_out_3, or_2_out_3;

  NOR nor_1 (.in_1(in_1), .in_2(in_2), .out_3(nor_1_out_3));
  NOT not_1 (.in_1(in_3), .out_2(not_1_out_2));
  NOT not_2 (.in_1(in_4), .out_2(not_2_out_2));
  OR or_1 (.in_1(nor_1_out_3), .in_2(and_1_out_3), .out_3(or_1_out_3));
  AND and_1 (.in_1(in_2), .in_2(not_1_out_2), .out_3(and_1_out_3));
  AND and_2 (.in_1(in_3), .in_2(or_2_out_3), .out_3(and_2_out_3));
  OR or_2 (.in_1(in_1), .in_2(not_2_out_2), .out_3(or_2_out_3));
  OR or_3 (.in_1(or_1_out_3), .in_2(and_2_out_3), .out_3(out_5));
endmodule

module d_d0 (
  input  in_1,
  input  in_2,
  input  in_3,
  input  in_4,
  output out_5
);

  wire and_1_out_3, and_2_out_3, and_3_out_3, and_4_out_3, and_5_out_3, and_6_out_3, not_1_out_2,
       not_2_out_2, not_3_out_2, not_4_out_2, or_1_out_3, or_2_out_3, or_3_out_3, xor_1_out_3;

  NOT not_1 (.in_1(in_1), .out_2(not_1_out_2));
  NOT not_2 (.in_1(in_2), .out_2(not_2_out_2));
  NOT not_3 (.in_1(in_3), .out_2(not_3_out_2));
  NOT not_4 (.in_1(in_4), .out_2(not_4_out_2));
  AND and_1 (.in_1(not_1_out_2), .in_2(not_2_out_2), .out_3(and_1_out_3));
  AND and_2 (.in_1(and_1_out_3), .in_2(not_4_out_2), .out_3(and_2_out_3));
  AND and_3 (.in_1(in_1), .in_2(in_4), .out_3(and_3_out_3));
  OR or_1 (.in_1(and_3_out_3), .in_2(and_2_out_3), .out_3(or_1_out_3));
  XOR xor_1 (.in_1(in_1), .in_2(in_2), .out_3(xor_1_out_3));
  AND and_4 (.in_1(or_1_out_3), .in_2(not_3_out_2), .out_3(and_4_out_3));
  OR or_2 (.in_1(not_1_out_2), .in_2(not_4_out_2), .out_3(or_2_out_3));
  AND and_5 (.in_1(or_2_out_3), .in_2(in_3), .out_3(and_5_out_3));
  AND and_6 (.in_1(xor_1_out_3), .in_2(in_4), .out_3(and_6_out_3));
  OR or_3 (.in_1(and_4_out_3), .in_2(and_5_out_3), .out_3(or_3_out_3));
  OR or_4 (.in_1(and_6_out_3), .in_2(or_3_out_3), .out_3(out_5));
endmodule

module e_d1 (
  input  in_1,
  input  in_2,
  input  in_3,
  input  in_4,
  output out_5
);

  wire and_1_out_3, and_2_out_3, nor_1_out_3, not_1_out_2, not_2_out_2, or_1_out_3, or_2_out_3;

  NOR nor_1 (.in_1(in_1), .in_2(in_2), .out_3(nor_1_out_3));
  NOT not_1 (.in_1(in_3), .out_2(not_1_out_2));
  NOT not_2 (.in_1(in_4), .out_2(not_2_out_2));
  OR or_1 (.in_1(nor_1_out_3), .in_2(and_1_out_3), .out_3(or_1_out_3));
  AND and_1 (.in_1(in_2), .in_2(not_1_out_2), .out_3(and_1_out_3));
  AND and_2 (.in_1(in_3), .in_2(or_2_out_3), .out_3(and_2_out_3));
  OR or_2 (.in_1(in_1), .in_2(not_2_out_2), .out_3(or_2_out_3));
  OR or_3 (.in_1(or_1_out_3), .in_2(and_2_out_3), .out_3(out_5));
endmodule

module e_d0 (
  input  in_1,
  input  in_2,
  input  in_3,
  input  in_4,
  output out_5
);

  wire and_1_out_3, and_2_out_3, and_3_out_3, and_4_out_3, and_5_out_3, and_6_out_3, and_7_out_3,
       not_1_out_2, not_2_out_2, not_3_out_2, not_4_out_2, or_1_out_3, or_2_out_3;

  NOT not_1 (.in_1(in_1), .out_2(not_1_out_2));
  NOT not_2 (.in_1(in_2), .out_2(not_2_out_2));
  NOT not_3 (.in_1(in_3), .out_2(not_3_out_2));
  NOT not_4 (.in_1(in_4), .out_2(not_4_out_2));
  AND and_1 (.in_1(not_2_out_2), .in_2(not_4_out_2), .out_3(and_1_out_3));
  OR or_1 (.in_1(and_1_out_3), .in_2(and_2_out_3), .out_3(or_1_out_3));
  AND and_2 (.in_1(in_2), .in_2(in_3), .out_3(and_2_out_3));
  AND and_3 (.in_1(in_1), .in_2(not_2_out_2), .out_3(and_3_out_3));
  AND and_4 (.in_1(not_1_out_2), .in_2(or_1_out_3), .out_3(and_4_out_3));
  AND and_5 (.in_1(and_3_out_3), .in_2(not_3_out_2), .out_3(and_5_out_3));
  AND and_6 (.in_1(and_5_out_3), .in_2(in_4), .out_3(and_6_out_3));
  OR or_2 (.in_1(and_6_out_3), .in_2(and_4_out_3), .out_3(or_2_out_3));
  AND and_7 (.in_1(not_4_out_2), .in_2(in_3), .out_3(and_7_out_3));
  OR or_3 (.in_1(or_2_out_3), .in_2(and_7_out_3), .out_3(out_5));
endmodule

module f_d1 (
  input  in_1,
  input  in_2,
  input  in_3,
  input  in_4,
  output out_5
);

  wire and_1_out_3, and_2_out_3, nor_1_out_3, not_1_out_2, not_2_out_2, or_1_out_3, or_2_out_3;

  NOR nor_1 (.in_1(in_1), .in_2(in_2), .out_3(nor_1_out_3));
  NOT not_1 (.in_1(in_3), .out_2(not_1_out_2));
  NOT not_2 (.in_1(in_4), .out_2(not_2_out_2));
  OR or_1 (.in_1(nor_1_out_3), .in_2(and_1_out_3), .out_3(or_1_out_3));
  AND and_1 (.in_1(in_2), .in_2(not_1_out_2), .out_3(and_1_out_3));
  AND and_2 (.in_1(in_3), .in_2(or_2_out_3), .out_3(and_2_out_3));
  OR or_2 (.in_1(in_1), .in_2(not_2_out_2), .out_3(or_2_out_3));
  OR or_3 (.in_1(or_1_out_3), .in_2(and_2_out_3), .out_3(out_5));
endmodule

module f_d0 (
  input  in_1,
  input  in_2,
  input  in_3,
  input  in_4,
  output out_5
);

  wire and_1_out_3, and_2_out_3, and_3_out_3, and_4_out_3, nor_1_out_3, not_1_out_2, not_2_out_2, or_1_out_3,
       or_2_out_3, or_3_out_3;

  NOT not_1 (.in_1(in_1), .out_2(not_1_out_2));
  OR or_1 (.in_1(not_1_out_2), .in_2(in_2), .out_3(or_1_out_3));
  NOT not_2 (.in_1(in_2), .out_2(not_2_out_2));
  NOR nor_1 (.in_1(in_3), .in_2(in_4), .out_3(nor_1_out_3));
  AND and_1 (.in_1(in_1), .in_2(not_2_out_2), .out_3(and_1_out_3));
  AND and_2 (.in_1(or_1_out_3), .in_2(nor_1_out_3), .out_3(and_2_out_3));
  OR or_2 (.in_1(in_3), .in_2(in_4), .out_3(or_2_out_3));
  AND and_3 (.in_1(not_1_out_2), .in_2(in_2), .out_3(and_3_out_3));
  OR or_3 (.in_1(and_2_out_3), .in_2(and_4_out_3), .out_3(or_3_out_3));
  AND and_4 (.in_1(and_1_out_3), .in_2(or_2_out_3), .out_3(and_4_out_3));
  OR or_4 (.in_1(and_3_out_3), .in_2(or_3_out_3), .out_3(out_5));
endmodule

module g_d0 (
  input  in_1,
  input  in_2,
  input  in_3,
  input  in_4,
  output out_5
);

  wire and_1_out_3, not_1_out_2, xor_1_out_3;

  XOR xor_1 (.in_1(in_2), .in_2(in_3), .out_3(xor_1_out_3));
  AND and_1 (.in_1(in_3), .in_2(not_1_out_2), .out_3(and_1_out_3));
  NOT not_1 (.in_1(in_4), .out_2(not_1_out_2));
  OR or_1 (.in_1(xor_1_out_3), .in_2(and_1_out_3), .out_3(out_5));
  // also tied to GND on the sheet: in_1
endmodule
