// Logisim project Gates.circ as structural Verilog: 7 circuits, main circuit main
module main (
  input  in_1,
  input  in_2,
  input  in_3,
  input  in_4,
  input  in_5,
  input  in_6,
  input  in_7,
  input  in_8,
  input  in_9,
  output out_10,
  output out_11,
  output out_12,
  output out_13
);

  wire transistor_3_out, transistor_4_out, transistor_7_out, transistor_14_out, transistor_17_out,
       transistor_18_out;

  Transistor transistor_1 (.in(1'b1), .out(out_11), .gate(in_4));
  Transistor #(.\type ("n")) transistor_2 (.in(1'b0), .out(out_11), .gate(in_4));
  Transistor #(.\type ("n")) transistor_3 (.in(transistor_4_out), .out(transistor_3_out), .gate(in_7));
  Transistor #(.\type ("n")) transistor_4 (.in(1'b0), .out(transistor_4_out), .gate(in_9));
  Transistor transistor_5 (.in(1'b1), .out(out_10), .gate(in_2));
  Transistor #(.\type ("n")) transistor_6 (.in(transistor_7_out), .out(out_10), .gate(in_2));
  Transistor #(.\type ("n")) transistor_7 (.in(1'b0), .out(transistor_7_out), .gate(in_5));
  Transistor transistor_8 (.in(1'b1), .out(transistor_3_out), .gate(in_7));
  Transistor transistor_9 (.in(1'b1), .out(out_10), .gate(in_5));
  Transistor transistor_10 (.in(1'b1), .out(transistor_3_out), .gate(in_9));
  Transistor transistor_11 (.in(1'b1), .out(out_13), .gate(transistor_3_out));
  Transistor #(.\type ("n")) transistor_12 (.in(1'b0), .out(out_13), .gate(transistor_3_out));
  Transistor #(.\type ("n")) transistor_13 (.in(1'b0), .out(out_12), .gate(in_1));
  Transistor transistor_14 (.in(1'b1), .out(transistor_14_out), .gate(in_1));
  Transistor transistor_15 (.in(transistor_14_out), .out(out_12), .gate(in_3));
  Transistor #(.\type ("n")) transistor_16 (.in(1'b0), .out(out_12), .gate(in_3));
  Transistor transistor_17 (.in(1'b1), .out(transistor_17_out), .gate(in_6));
  Transistor transistor_18 (.in(transistor_17_out), .out(transistor_18_out), .gate(in_8));
  Transistor #(.\type ("n")) transistor_19 (.in(1'b0), .out(transistor_18_out), .gate(in_6));
  Transistor #(.\type ("n")) transistor_20 (.in(1'b0), .out(transistor_18_out), .gate(in_8));

  // Notes on the sheet:
  //   NOT
  //   AND
  //   NAND
  //   NOR
  //   OR
endmodule

module NOT (
  input  in_1,
  output out_2
);

  Transistor transistor_1 (.in(1'b1), .out(out_2), .gate(in_1));
  Transistor #(.\type ("n")) transistor_2 (.in(1'b0), .out(out_2), .gate(in_1));

  // Notes on the sheet:
  //   NOT
endmodule

module NAND (
  input  in_1,
  input  in_2,
  output out_3
);

  wire transistor_3_out;

  Transistor transistor_1 (.in(1'b1), .out(out_3), .gate(in_1));
  Transistor #(.\type ("n")) transistor_2 (.in(transistor_3_out), .out(out_3), .gate(in_1));
  Transistor #(.\type ("n")) transistor_3 (.in(1'b0), .out(transistor_3_out), .gate(in_2));
  Transistor transistor_4 (.in(1'b1), .out(out_3), .gate(in_2));

  // Notes on the sheet:
  //   NAND
endmodule

module NOR (
  input  in_1,
  input  in_2,
  output out_3
);

  wire transistor_2_out;

  Transistor #(.\type ("n")) transistor_1 (.in(1'b0), .out(out_3), .gate(in_1));
  Transistor transistor_2 (.in(1'b1), .out(transistor_2_out), .gate(in_1));
  Transistor transistor_3 (.in(transistor_2_out), .out(out_3), .gate(in_2));
  Transistor #(.\type ("n")) transistor_4 (.in(1'b0), .out(out_3), .gate(in_2));

  // Notes on the sheet:
  //   NOR
endmodule

module AND (
  input  in_1,
  input  in_2,
  output out_3
);

  wire transistor_1_out, transistor_3_out;

  Transistor transistor_1 (.in(1'b1), .out(transistor_1_out), .gate(in_1));
  Transistor #(.\type ("n")) transistor_2 (.in(transistor_3_out), .out(transistor_1_out), .gate(in_1));
  Transistor #(.\type ("n")) transistor_3 (.in(1'b0), .out(transistor_3_out), .gate(in_2));
  Transistor transistor_4 (.in(1'b1), .out(transistor_1_out), .gate(in_2));
  Transistor transistor_5 (.in(1'b1), .out(out_3), .gate(transistor_1_out));
  Transistor #(.\type ("n")) transistor_6 (.in(1'b0), .out(out_3), .gate(transistor_1_out));

  // Notes on the sheet:
  //   AND
endmodule

module OR (
  input  in_1,
  input  in_2,
  output out_3
);

  wire transistor_1_out, transistor_2_out;

  Transistor #(.\type ("n")) transistor_1 (.in(1'b0), .out(transistor_1_out), .gate(in_1));
  Transistor transistor_2 (.in(1'b1), .out(transistor_2_out), .gate(in_1));
  Transistor transistor_3 (.in(transistor_2_out), .out(transistor_1_out), .gate(in_2));
  Transistor transistor_4 (.in(1'b1), .out(out_3), .gate(transistor_1_out));
  Transistor #(.\type ("n")) transistor_5 (.in(1'b0), .out(out_3), .gate(transistor_1_out));
  Transistor #(.\type ("n")) transistor_6 (.in(1'b0), .out(transistor_1_out), .gate(in_2));
endmodule

module XOR (
  input  in_1,
  input  in_2,
  output out_3
);

  wire nand_1_out_3, or_1_out_3;

  NAND nand_1 (.in_1(in_1), .in_2(in_2), .out_3(nand_1_out_3));
  OR or_1 (.in_1(in_1), .in_2(in_2), .out_3(or_1_out_3));
  AND and_1 (.in_1(nand_1_out_3), .in_2(or_1_out_3), .out_3(out_3));

  // Notes on the sheet:
  //   XOR
endmodule
