// Logisim project Latches.circ as structural Verilog
module SR_NOR_LATCH (
  input  in_1,
  input  in_2,
  output out_3,
  output out_4
);

  nor nor_1 (out_3, in_1, out_4);
  nor nor_2 (out_4, out_3, in_2);
endmodule

module SR_NAND_LATCH (
  input  in_1,
  input  in_2,
  output out_3,
  output out_4
);

  nand nand_1 (out_3, in_1, out_4);
  nand nand_2 (out_4, out_3, in_2);
endmodule

module D_NAND_LATCH (
  input  in_1,
  input  in_2,
  output out_3,
  output out_4
);

  wire nand_1_out, nand_2_out, not_1_out;

  not not_1 (not_1_out, in_1);
  nand nand_1 (nand_1_out, in_1, in_2);
  nand nand_2 (nand_2_out, not_1_out, in_2);
  nand nand_3 (out_3, nand_1_out, out_4);
  nand nand_4 (out_4, out_3, nand_2_out);
endmodule

module D_flip_flop (
  input  in_1,
  input  in_2,
  output out_3,
  output out_4
);

  wire d_nand_latch_1_out_3, not_1_out;

  D_NAND_LATCH d_nand_latch_1 (.in_1(in_1), .in_2(in_2), .out_3(d_nand_latch_1_out_3));  // open: out_4
  D_NAND_LATCH d_nand_latch_2 (.in_1(d_nand_latch_1_out_3), .in_2(not_1_out), .out_3(out_3), .out_4(out_4));
  not not_1 (not_1_out, in_2);
endmodule
