# Fritzing sketch knight rider (saved by Fritzing 0.9.3b)
circuit board: 10cm x 5cm
breadboards: 1

parts:
  U1 = 555 Timer [package="DIP8 [THT]"]
  VCC1 = Battery
  C1 = Ceramic Capacitor [capacitance=100nF package="100 mil [THT, multilayer]"]
  LED3 = LED - 5mm [color="Green (560nm)" package="5 mm [THT]"]
  R3 = Resistor [tolerance=±5% resistance=220 package=THT]
  LED4 = LED - 5mm [color="Green (560nm)" package="5 mm [THT]"]
  LED5 = LED - 5mm [color="Green (560nm)" package="5 mm [THT]"]
  LED6 = LED - 5mm [color="Green (560nm)" package="5 mm [THT]"]
  LED7 = LED - 5mm [color="Green (560nm)" package="5 mm [THT]"]
  LED8 = LED - 5mm [color="Green (560nm)" package="5 mm [THT]"]
  R4 = Resistor [tolerance=±5% resistance=100 package=THT]
  R5 = Resistor [tolerance=±5% resistance=100 package=THT]
  R6 = Resistor [tolerance=±5% resistance=100 package=THT]
  R7 = Resistor [tolerance=±5% resistance=100 package=THT]
  R8 = Resistor [tolerance=±5% resistance=100 package=THT]
  R9 = Resistor [tolerance=±5% resistance=100 package=THT]
  R10 = Resistor [tolerance=±5% resistance=100 package=THT]
  R11 = Resistor [tolerance=±5% resistance=100 package=THT]
  R12 = Resistor [tolerance=±5% resistance=220 package=THT]
  R13 = Resistor [tolerance=±5% resistance=50k package=THT]
  R14 = Resistor [tolerance=±5% resistance=1k package=THT]
  IC1 = IC, DIP package, 16 pins [chip_label="4017 IC"]

nets:
  N1: U1.Ground, VCC1.+, C1.1, LED3.cathode, LED4.cathode, LED5.cathode, LED6.cathode, LED7.cathode, LED8.cathode, IC1.pin8, IC1.pin13, IC1.pin15
  N2: U1.Trigger, U1.Threshold, C1.0, R14.Pin_1
  N3: U1.Output, IC1.pin14
  N4: U1.Reset, U1.Vcc_Supply_Voltage, VCC1.-, R13.Pin_0
  N5: U1.Discharge, R13.Pin_1, R14.Pin_0
  N6: LED3.anode, R3.Pin_1
  N7: R3.Pin_0, IC1.pin3
  N8: LED4.anode, R4.Pin_1, R5.Pin_1
  N9: LED5.anode, R6.Pin_1, R7.Pin_1
  N10: LED6.anode, R8.Pin_1, R9.Pin_1
  N11: LED7.anode, R11.Pin_1
  N12: LED8.anode, R12.Pin_1
  N13: R4.Pin_0, IC1.pin2
  N14: R5.Pin_0, IC1.pin11
  N15: R6.Pin_0, IC1.pin4
  N16: R7.Pin_0, IC1.pin9
  N17: R8.Pin_0, IC1.pin7
  N18: R9.Pin_0, IC1.pin6
  N19: R10.Pin_0, IC1.pin10
  N20: R11.Pin_0, IC1.pin5
  N21: R12.Pin_0, IC1.pin1
